// Logisim project CPU RiscV.circ as structural Verilog
module main (
  input  in_1
);

  wire alu_1_f_zero, alu_control_1_beq_bne, and_1_out, and_2_out, and_3_out, clock_1_out,
       control_unit_1_alu_src, control_unit_1_branch, control_unit_1_jump_reg, control_unit_1_mem_read,
       control_unit_1_mem_to_reg, control_unit_1_mem_write, control_unit_1_reg_write, control_unit_1_sum_pc,
       exmem_1_branch_out, exmem_1_jalr_ou_jal_out, exmem_1_mem_read_out, exmem_1_mem_to_reg_out,
       exmem_1_mem_write_out, exmem_1_reg_write_out, exmem_1_zero_out, hazard_1_stall, idex_1_alu_src_out,
       idex_1_branch_out, idex_1_jumpreg_out, idex_1_mem_read_out, idex_1_mem_to_reg_out,
       idex_1_memwrite_out, idex_1_reg_write_out, idex_1_soma_pc_out, memwb_1_memtoreg_out,
       memwb_1_regwrite_out, not_1_out, not_2_out, or_1_out, undriven;
  wire [1:0] control_unit_1_alu_op, forward_1_forwarda, forward_1_forwardb, idex_1_alu_op_out;
  wire [2:0] control_unit_1_s_funct3, idex_1_funct3_out;
  wire [3:0] alu_control_1_alu_out;
  wire [4:0] exmem_1_rd_out, idex_1_rd_out, idex_1_rs1_out, idex_1_rs2_out, ifid_1_p7, ifid_1_p8, ifid_1_p9,
       memwb_1_rd_out;
  wire [6:0] control_unit_1_s_funct7, control_unit_1_s_opcode, idex_1_funct7_out, idex_1_opcode_out;
  wire [23:0] exmem_1_alu_result_out;
  wire [31:0] alu_1_resultado, exmem_1_new_pc_out, exmem_1_read2_out, idex_1_immediate_out, idex_1_pc_out,
       idex_1_read1_out, idex_1_read2_out, ifid_1_p5, ifid_1_p6, immediate_generator_1_immediate,
       memwb_1_aluresult_out, memwb_1_mem_data_out, multiplexer_1_out, multiplexer_2_out, multiplexer_3_out,
       multiplexer_4_out, multiplexer_5_out, multiplexer_6_out, multiplexer_7_out, multiplexer_8_out,
       pc4_1_pc_out, ram_1_dout, registerfile_1_read_data_1, registerfile_1_read_data_2, rom_1_data,
       somador_1_z;
  wire [31:24] exmem_1_alu_result_out_2;

  Clock clock_1 (.out(clock_1_out));
  Multiplexer #(.width(32)) multiplexer_1 (
    .in0(pc4_1_pc_out), .in1(exmem_1_new_pc_out), .out(multiplexer_1_out), .sel(or_1_out));
  PC4 pc4_1 (
    .clk(clock_1_out), .reset(undriven), .PC_in(multiplexer_1_out), .Write_Enable(not_1_out),
    .PC_out(pc4_1_pc_out));
  ROM #(.addrWidth(24), .dataWidth(32)) rom_1 (.addr(pc4_1_pc_out[23:0]), .data(rom_1_data));
  not not_1 (not_1_out, hazard_1_stall);
  // IFID ifid_1: pin names not known; wires that end beside it: clock_1_out, pc4_1_pc_out, not_1_out, rom_1_data, ifid_1_p5, ifid_1_p6, ifid_1_p7, ifid_1_p8, ifid_1_p9
  Hazard hazard_1 (
    .clk(clock_1_out), .Mem_Read_in(idex_1_mem_read_out), .Rd_EX(idex_1_rd_out), .Rs1(ifid_1_p7),
    .Rs2(ifid_1_p8), .stall(hazard_1_stall));
  Control_Unit control_unit_1 (
    .instruction(ifid_1_p6), .Stall(hazard_1_stall), .Alu_Src(control_unit_1_alu_src),
    .Reg_Write(control_unit_1_reg_write), .Mem_To_Reg(control_unit_1_mem_to_reg),
    .Mem_Read(control_unit_1_mem_read), .Mem_Write(control_unit_1_mem_write), .Branch(control_unit_1_branch),
    .Sum_PC(control_unit_1_sum_pc), .Alu_Op(control_unit_1_alu_op), .S_funct7(control_unit_1_s_funct7),
    .S_funct3(control_unit_1_s_funct3), .S_opcode(control_unit_1_s_opcode), .Jump_Reg(control_unit_1_jump_reg));
  RegisterFile registerfile_1 (
    .Read_Register_1(ifid_1_p7), .Read_Register_2(ifid_1_p8), .Write_Register(memwb_1_rd_out),
    .Write_Data(multiplexer_8_out), .Reg_Write(memwb_1_regwrite_out), .clk(clock_1_out),
    .Read_Data_1(registerfile_1_read_data_1), .Read_Data_2(registerfile_1_read_data_2));
  Immediate_Generator immediate_generator_1 (.instruction(ifid_1_p6), .immediate(immediate_generator_1_immediate));
  IDEX idex_1 (
    .clk(clock_1_out), .ALU_Src_in(control_unit_1_alu_src), .ALU_Op_in(control_unit_1_alu_op),
    .funct3_in(control_unit_1_s_funct3), .funct7_in(control_unit_1_s_funct7), .PC_in(ifid_1_p5),
    .Soma_PC_in(control_unit_1_sum_pc), .Branch_in(control_unit_1_branch),
    .Mem_Write_in(control_unit_1_mem_write), .Mem_Read_in(control_unit_1_mem_read),
    .Reg_Write_in(control_unit_1_reg_write), .Mem_To_Reg_in(control_unit_1_mem_to_reg),
    .read1_in(registerfile_1_read_data_1), .read2_in(registerfile_1_read_data_2),
    .immediate_in(immediate_generator_1_immediate), .Rd_in(ifid_1_p9), .Opcode_in(control_unit_1_s_opcode),
    .JumpReg_in(control_unit_1_jump_reg), .Rs1_In(ifid_1_p7), .Rs2_In(ifid_1_p8),
    .ALU_Src_out(idex_1_alu_src_out), .ALU_Op_out(idex_1_alu_op_out), .funct3_out(idex_1_funct3_out),
    .funct7_out(idex_1_funct7_out), .PC_out(idex_1_pc_out), .Soma_PC_out(idex_1_soma_pc_out),
    .Branch_out(idex_1_branch_out), .MemWrite_out(idex_1_memwrite_out), .Mem_Read_out(idex_1_mem_read_out),
    .Reg_Write_out(idex_1_reg_write_out), .Mem_To_Reg_out(idex_1_mem_to_reg_out),
    .read1_out(idex_1_read1_out), .read2_out(idex_1_read2_out), .immediate_out(idex_1_immediate_out),
    .Rd_out(idex_1_rd_out), .Opcode_out(idex_1_opcode_out), .JumpReg_out(idex_1_jumpreg_out),
    .Rs1_out(idex_1_rs1_out), .Rs2_out(idex_1_rs2_out));
  not not_2 (not_2_out, idex_1_alu_src_out);
  and and_1 (and_1_out, not_2_out, idex_1_soma_pc_out);
  Multiplexer #(.width(32)) multiplexer_2 (
    .in0(idex_1_read2_out), .in1(idex_1_immediate_out), .out(multiplexer_2_out), .sel(idex_1_alu_src_out));
  Multiplexer #(.width(32)) multiplexer_3 (
    .in0(idex_1_pc_out), .in1(idex_1_read1_out), .out(multiplexer_3_out), .sel(idex_1_jumpreg_out));
  Multiplexer #(.width(32)) multiplexer_4 (
    .in0(idex_1_read1_out), .in1(idex_1_pc_out), .out(multiplexer_4_out), .sel(idex_1_soma_pc_out));
  Multiplexer #(.width(32)) multiplexer_5 (
    .in0(multiplexer_2_out), .in1(32'h1), .out(multiplexer_5_out), .sel(and_1_out));
  ALU_Control alu_control_1 (
    .Funct7(idex_1_funct7_out), .Funct3(idex_1_funct3_out), .Op_code(idex_1_opcode_out),
    .Alu_Op(idex_1_alu_op_out), .ALU_Out(alu_control_1_alu_out), .Beq_Bne(alu_control_1_beq_bne));
  Multiplexer #(.select(2), .width(32)) multiplexer_6 (
    .in0(multiplexer_4_out), .in1(multiplexer_8_out),
    .in2({exmem_1_alu_result_out_2, exmem_1_alu_result_out}), .out(multiplexer_6_out),
    .sel(forward_1_forwarda));  // open: in3
  Somador somador_1 (.A(multiplexer_3_out), .B(idex_1_immediate_out), .Z(somador_1_z));
  Multiplexer #(.select(2), .width(32)) multiplexer_7 (
    .in0(multiplexer_5_out), .in1(multiplexer_8_out),
    .in2({exmem_1_alu_result_out_2, exmem_1_alu_result_out}), .out(multiplexer_7_out),
    .sel(forward_1_forwardb));  // open: in3
  ALU alu_1 (
    .A(multiplexer_6_out), .B(multiplexer_7_out), .controle(alu_control_1_alu_out),
    .resultado(alu_1_resultado), .f_zero(alu_1_f_zero));
  Forward forward_1 (
    .clk(clock_1_out), .reg_Write_WB(memwb_1_regwrite_out), .regWrite_MEM(exmem_1_reg_write_out),
    .Rs1(idex_1_rs1_out), .Rs2(idex_1_rs2_out), .Rd_WB(memwb_1_rd_out), .Rd_Mem(exmem_1_rd_out),
    .forwardA(forward_1_forwarda), .forwardB(forward_1_forwardb));
  and and_2 (and_2_out, alu_1_f_zero, alu_control_1_beq_bne);
  EXMEM exmem_1 (
    .clk(clock_1_out), .Branch_in(idex_1_branch_out), .Mem_Write_in(idex_1_memwrite_out),
    .Mem_Read_in(idex_1_mem_read_out), .Reg_Write_in(idex_1_reg_write_out),
    .Mem_To_Reg_in(idex_1_mem_to_reg_out), .New_PC_in(somador_1_z), .Zero_in(and_2_out),
    .ALU_result_in(alu_1_resultado), .read2_in(idex_1_read2_out), .Rd_in(idex_1_rd_out),
    .Jalr_ou_Jal_in(and_1_out), .Branch_out(exmem_1_branch_out), .Mem_Write_out(exmem_1_mem_write_out),
    .Mem_Read_out(exmem_1_mem_read_out), .Reg_Write_out(exmem_1_reg_write_out),
    .Mem_To_Reg_out(exmem_1_mem_to_reg_out), .New_PC_out(exmem_1_new_pc_out), .Zero_out(exmem_1_zero_out),
    .ALU_result_out({exmem_1_alu_result_out_2, exmem_1_alu_result_out}), .read2_out(exmem_1_read2_out),
    .Rd_out(exmem_1_rd_out), .Jalr_ou_Jal_out(exmem_1_jalr_ou_jal_out));
  and and_3 (and_3_out, exmem_1_branch_out, exmem_1_zero_out);
  or or_1 (or_1_out, and_3_out, exmem_1_jalr_ou_jal_out);
  RAM #(.addrWidth(24), .dataWidth(32)) ram_1 (
    .addr(exmem_1_alu_result_out), .we(exmem_1_mem_write_out), .oe(exmem_1_mem_read_out), .clk(clock_1_out),
    .din(exmem_1_read2_out), .dout(ram_1_dout));
  MEMWB memwb_1 (
    .CLK(clock_1_out), .RegWrite_in(exmem_1_reg_write_out), .MemToReg_in(exmem_1_mem_to_reg_out),
    .Mem_data_in(ram_1_dout), .ALUresult_in({exmem_1_alu_result_out_2, exmem_1_alu_result_out}),
    .Rd_in(exmem_1_rd_out), .RegWrite_out(memwb_1_regwrite_out), .MemToReg_out(memwb_1_memtoreg_out),
    .Mem_data_out(memwb_1_mem_data_out), .ALUresult_out(memwb_1_aluresult_out), .Rd_out(memwb_1_rd_out));
  Multiplexer #(.width(32)) multiplexer_8 (
    .in0(memwb_1_aluresult_out), .in1(memwb_1_mem_data_out), .out(multiplexer_8_out),
    .sel(memwb_1_memtoreg_out));
endmodule

// VHDL entity ALU, as the project stores it:
library IEEE;
use IEEE.STD_LOGIC_1164.ALL;
use ieee.numeric_std.ALL;
use IEEE.std_logic_unsigned.ALL;

entity ALU is
    port(
    A, B      	: in std_logic_vector(31 downto 0);  -- Operandos A e B de 32 bits da ALU
    controle   : in std_logic_vector(3 downto 0);   -- Entrada responsável por determinar a operação da ALU
    resultado  : out std_logic_vector(31 downto 0); -- Resultado da operação feita pela ALU
    f_zero     : out std_logic);                    -- Flag indicadora de resultado igual a zero na operacão da ALU
end ALU;

architecture Behavioral of ALU is

signal resultado_temp : std_logic_vector(31 downto 0);  -- Vetor auxiliar que armazena o resultado da operação

begin
	
    resultado_temp <= (A + B) when controle = "0010" else                  -- Operação de Soma
    			   	 (A - B) when controle = "0110" else                  -- Operação de Subtração
    			   	 (A XOR B) when controle = "0101" else                -- Operação XOR (Exclusive OR)
    			   	 (A OR B) when controle = "0001" else                 -- Operação OR 
    			   	 (A AND B) when controle = "0000" else                -- Operação AND 
    			   	 (std_logic_vector(shift_left(unsigned(A), to_integer(unsigned(B))))) when controle = "0011" else   	-- Operação de Shift Left
    			   	 (std_logic_vector(shift_right(unsigned(A), to_integer(unsigned(B))))) when controle = "0111";    		-- Operação de Shift Right 
        			
    resultado <= resultado_temp;                            			    			-- Atribuição do valor final à saída resultado
    f_zero <= '1' when resultado_temp = "00000000000000000000000000000000" else '0';	-- Sinalização se o resultado é zero 
    														    			-- (Se zero_sig(32) for '0', f_zero é '1', caso contrário, f_zero é '0')
end Behavioral;

// VHDL entity ALU_Control, as the project stores it:
library IEEE;
use IEEE.STD_LOGIC_1164.ALL;

entity ALU_Control is
    port(
        Funct7    		: IN std_logic_vector(6 downto 0);    	 -- Entrada do funct7
        Funct3    		: IN std_logic_vector(2 downto 0);    	 -- Entrada do funct3
        Op_code    		: IN std_logic_vector(6 downto 0);   	 -- Entrada do opcode
        Alu_Op   		: IN std_logic_vector(1 downto 0);       -- Entrada de códigos de operação da ALU (2 bits)
        ALU_Out	: OUT std_logic_vector(3 downto 0);      -- Saída do controle da ALU (4 bits)
        Beq_Bne     : OUT std_logic					 -- Sinal de controle para verificação de Beq ou Bne
        );
end ALU_Control;

architecture Behavioral of ALU_Control is
begin

	ALU_Out <= "0010" when Alu_Op = "00" else 	-- Operação de Load
			 	 "0110" when Alu_Op = "01" else 	-- Operação de Branch
			 	 "0010" when Funct7 = "0000000" and Funct3 = "000" else 	-- Operação de Soma
			 	 "0110" when Funct7 = "0100000" and Funct3 = "000" else 	-- Operação de Subtração
			 	 "0011" when Funct7 = "0000000" and Funct3 = "001" else 	-- Operação de Shift Left
			 	 "0101" when Funct7 = "0000000" and Funct3 = "100" else 	-- Operação XOR
			 	 "0111" when Funct7 = "0000000" and Funct3 = "101" else 	-- Operação de Shift Right
			 	 "0001" when Funct7 = "0000000" and Funct3 = "110" else 	-- Operação OR
			 	 "0000" when Funct7 = "0000000" and Funct3 = "111"; 		-- Operação AND
	Beq_Bne <= '1' when op_code="1100011" and Funct3="000" else '0';			-- '1' quando a instrução for Beq
	 
end Behavioral;

// VHDL entity Control_Unit, as the project stores it:
library IEEE;
use IEEE.STD_LOGIC_1164.ALL;

entity Control_Unit is
    port(
        instruction                	: IN  std_logic_vector(31 downto 0);  -- Entrada da Instrução
        Stall                			: IN  std_logic;  				   -- Entrada do Hazard
        Alu_Src, Reg_Write, Mem_To_Reg 	: OUT std_logic;                      -- Sinais de Controle (1 Bit)
        Mem_Read, Mem_Write, Branch  	: OUT std_logic;                      -- Sinais de Controle (1 Bit)
        Sum_PC 					: OUT std_logic;			   	   -- Sinais de Controle (1 Bit)	
        Alu_Op		               	: OUT std_logic_vector(1 downto 0);   -- Saída da Operação da ALU (2 Bits)
        S_funct7 					: OUT std_logic_vector(6 downto 0);   -- Saída do Funct7
        S_funct3 					: OUT std_logic_vector(2 downto 0);   -- Saída do Funct3
        S_opcode 					: OUT std_logic_vector(6 downto 0);   -- Saída do Opcode
        Jump_Reg					: OUT std_logic);				   -- Indica quando a instrução é jalr	
end Control_Unit;

architecture Behavioral of Control_Unit is

signal opcode : std_logic_vector(6 downto 0);	-- Opcode da Instrução
signal funct7 : std_logic_vector(6 downto 0);	-- Funct7 da Instrução
signal funct3 : std_logic_vector(2 downto 0);	-- Funct3 da Instrução


begin
	-- Definição do Opcode da Instrução
	opcode(0) <= instruction(0);
	opcode(1) <= instruction(1);
	opcode(2) <= instruction(2);
	opcode(3) <= instruction(3);
	opcode(4) <= instruction(4);
	opcode(5) <= instruction(5);
	opcode(6) <= instruction(6);
	Sum_PC <= '0'; 
	Jump_Reg <= '0';

	process(Stall)
	begin
		IF (Stall = '1') THEN
			Alu_Src <= '0';
			Reg_Write <= '0';
			Mem_To_Reg <= '0';
			Mem_Reaad <= '0';
			Mem_Write <= '0';
			Branch <= '0';
			Sum_PC <= '0';
			Jump_Reg <= '0';
		end if; 
	end process;
	-- Definição das Funct7, Funct3 e dos Sinais de Controle de acordo com o opcode.
	process(opcode)
	begin
		IF (opcode = "0110011") THEN		-- R-Type Instruction
			funct7(6) <= instruction(31);
			funct7(5) <= instruction(30);
			funct7(4) <= instruction(29);
			funct7(3) <= instruction(28);
			funct7(2) <= instruction(27);
			funct7(1) <= instruction(26);
			funct7(0) <= instruction(25);
			funct3(2) <= instruction (14);
			funct3(1) <= instruction (13);
			funct3(0) <= instruction (12);
			Alu_Src <= '0'; 			
			Reg_Write <= '1';
			Mem_To_Reg <= '0';
			Mem_Read <= '0';
			Mem_Write <= '0';
			Branch <= '0';
			Alu_Op <= "10";
		END IF;
		IF (opcode = "0010011") THEN		-- I-Type Instruction (ADDi, ANDi, ORi, XORi, SLTi)
			funct7(6) <= '0';
			funct7(5) <= '0';
			funct7(4) <= '0';
			funct7(3) <= '0';
			funct7(2) <= '0';
			funct7(1) <= '0';
			funct7(0) <= '0';
			funct3(2) <= instruction (14);
			funct3(1) <= instruction (13);
			funct3(0) <= instruction (12);
			Alu_Src <= '1'; 			
			Reg_Write <= '1';
			Mem_To_Reg <= '0';
			Mem_Read <= '0';
			Mem_Write <= '0';
			Branch <= '0';
			Alu_Op <= "10";
		END IF;
		IF (opcode = "0000011") THEN		-- I-Type Instruction (Load)
			funct7(6) <= '0';
			funct7(5) <= '0';
			funct7(4) <= '0';
			funct7(3) <= '0';
			funct7(2) <= '0';
			funct7(1) <= '0';
			funct7(0) <= '0';
			funct3(2) <= '0';
			funct3(1) <= '0';
			funct3(0) <= '0';
			Alu_Src <= '1'; 			
			Reg_Write <= '1';
			Mem_To_Reg <= '1';
			Mem_Read <= '1';
			Mem_Write <= '0';
			Branch <= '0';
			Alu_Op <= "00";
		END IF;
		IF (opcode = "1100111") THEN		-- I-Type Instruction (Jump) 
			funct7(6) <= '0';
			funct7(5) <= '0';
			funct7(4) <= '0';
			funct7(3) <= '0';
			funct7(2) <= '0';
			funct7(1) <= '0';
			funct7(0) <= '0';
			funct3(2) <= '0';
			funct3(1) <= '0';
			funct3(0) <= '0';
			Alu_Src <= '0'; 			
			Reg_Write <= '0';
			Mem_To_Reg <= '0';
			Mem_Read <= '0';
			Mem_Write <= '0';
			Branch <= '0';
			Sum_PC <= '1';
			Jump_Reg <= '1';
			Alu_Op <= "01";
		END IF;
		IF (opcode = "0100011") THEN		-- S-Type Instruction 
			funct7(6) <= '0';
			funct7(5) <= '0';
			funct7(4) <= '0';
			funct7(3) <= '0';
			funct7(2) <= '0';
			funct7(1) <= '0';
			funct7(0) <= '0';
			funct3(2) <= '0';
			funct3(1) <= '0';
			funct3(0) <= '0';
			Alu_Src <= '1'; 			
			Reg_Write <= '0';
			Mem_To_Reg <= '0';
			Mem_Read <= '0';
			Mem_Write <= '1';
			Branch <= '0';
			Alu_Op <= "00";
		END IF;
		IF (opcode = "1101111") THEN		-- UJ-Type Instruction (jal)
			funct7(6) <= '0';
			funct7(5) <= '0';
			funct7(4) <= '0';
			funct7(3) <= '0';
			funct7(2) <= '0';
			funct7(1) <= '0';
			funct7(0) <= '0';
			funct3(2) <= '0';
			funct3(1) <= '0';
			funct3(0) <= '0';
			Alu_Src <= '0'; 			
			Reg_Write <= '1';
			Mem_To_Reg <= '0';
			Mem_Read <= '0';
			Mem_Write <= '0';
			Branch <= '0';
			Sum_PC <= '1';
			Alu_Op <= "10";
		END IF;
		IF (opcode = "0110111") THEN		-- U-Type Instruction (lui - soma com imediato muito grande)
			funct7(6) <= '0';
			funct7(5) <= '0';
			funct7(4) <= '0';
			funct7(3) <= '0';
			funct7(2) <= '0';
			funct7(1) <= '0';
			funct7(0) <= '0';
			funct3(2) <= '0';
			funct3(1) <= '0';
			funct3(0) <= '0';
			Alu_Src <= '1'; 			
			Reg_Write <= '1';
			Mem_To_Reg <= '0';
			Mem_Read <= '0';
			Mem_Write <= '0';
			Branch <= '0';
			Alu_Op <= "10";
		END IF;
		IF (opcode = "0010111") THEN		-- U-Type Instruction (auipc, soma do pc com o imediato e guarda no registrador)
			funct7(6) <= '0';
			funct7(5) <= '0';
			funct7(4) <= '0';
			funct7(3) <= '0';
			funct7(2) <= '0';
			funct7(1) <= '0';
			funct7(0) <= '0';
			funct3(2) <= '0';
			funct3(1) <= '0';
			funct3(0) <= '0';
			Alu_Src <= '1'; 			
			Reg_Write <= '1';
			Mem_To_Reg <= '0';
			Mem_Read <= '0';
			Mem_Write <= '0';
			Branch <= '0';
			Sum_PC <= '1';
			Alu_Op <= "10";
		END IF;
		IF (opcode = "1100011") THEN		-- Sb-Type Instruction 
			funct7(6) <= '0';
			funct7(5) <= '0';
			funct7(4) <= '0';
			funct7(3) <= '0';
			funct7(2) <= '0';
			funct7(1) <= '0';
			funct7(0) <= '0';
			funct3(2) <= instruction (14);
			funct3(1) <= instruction (13);
			funct3(0) <= instruction (12);
			Alu_Src <= '0'; 			
			Reg_Write <= '0';
			Mem_To_Reg <= '0';
			Mem_Read <= '0';
			Mem_Write <= '0';
			Branch <= '1';
			Alu_Op <= "01";
		END IF;
	end process;
	S_funct7 <= funct7;
	S_funct3 <= funct3;
	S_opcode <= opcode;
end Behavioral;

// VHDL entity Immediate_Generator, as the project stores it:
library IEEE;
use IEEE.STD_LOGIC_1164.ALL;
USE IEEE.NUMERIC_STD.ALL;

entity Immediate_Generator is
    Port( 
        instruction: in std_logic_vector(31 downto 0);  	-- Entrada da Instrução 
        immediate: out std_logic_vector(31 downto 0)  		-- Saída do Valor Imediato
        );
end Immediate_Generator;

architecture Behavioral of Immediate_Generator is
    signal op_code       : std_logic_vector(6 downto 0);  		-- Sinal para armazenr o opcode da instrução
    signal S_imm  : std_logic_vector(31 downto 0) := "00000000000000000000000000000000";  -- Sinal auxiliar para definição do imediato

begin

    op_code <= instruction(6 downto 0);  -- Definição do opcode

    process(op_code)
    begin
        if (op_code = "0010011" or op_code = "0000011" or op_code = "1100111") then  	-- Tipo I 
            S_imm(11 downto 0)  <= instruction(31 downto 20);  					-- Seleciona o imediato 
            S_imm(31 downto 12) <= (others => instruction(31));  				-- Extensão do Bit de Sinal
        elsif (op_code = "1101111") then  									-- Tipo UJ 
            S_imm(20) <= instruction(31);  									-- Seleciona o imediato
            S_imm(10 downto 1) <= instruction(30 downto 21);					-- Seleciona o imediato
            S_imm(11) <= instruction(20);									-- Seleciona o imediato	
            S_imm(19 downto 12) <= instruction(19 downto 12);					-- Seleciona o imediato
            S_imm(31 downto 21) <= (others => instruction(31));					-- Extensão do Bit de Sinal
        elsif (op_code = "0110111" or op_code = "0010111") then										-- Tipo U 
        	  S_imm(31 downto 12) <= instruction(31 downto 12);  					-- Seleciona o imediato	
        elsif (op_code = "0100011") then  									-- Tipo S 
            S_imm(11 downto 5)  <= instruction(31 downto 25);  					-- Seleciona o imediato
            S_imm(4 downto 0)   <= instruction(11 downto 7);   					-- Seleciona o imediato
            S_imm(31 downto 12) <= (others => instruction(31));  				-- Extensão do Bit de Sinal
        elsif (op_code = "1100011") then  									-- Tipo SB
            S_imm(12)           <= instruction(31);          					-- Seleciona o imediato
            S_imm(11)           <= instruction(7);           					-- Seleciona o imediato
            S_imm(10 downto 5)  <= instruction(30 downto 25);  					-- Seleciona o imediato
            S_imm(4 downto 1)   <= instruction(11 downto 8);   					-- Seleciona o imediato
            S_imm(31 downto 13) <= (others => instruction(31));  				-- Extensão do Bit de Sinal
        end if;
    end process;

    immediate <= S_imm;  												-- Atribui o valor imeadiato à saída

end Behavioral;

// VHDL entity PC4, as the project stores it:
library IEEE;
use IEEE.STD_LOGIC_1164.ALL;
use ieee.numeric_std.ALL;
use IEEE.std_logic_unsigned.ALL;


ENTITY PC4 IS
  PORT (
    clk      : IN  std_logic;                    		-- Entrada do Clock
    reset    : IN  std_logic;                    		-- Entrada de Reset
    PC_in    : IN  std_logic_vector(31 DOWNTO 0); 	-- Entrada do endereço atual
    Write_Enable   : IN std_logic;               		-- Entrada de Habilitação de escrita no PC
    PC_out   : OUT std_logic_vector(31 DOWNTO 0)  	-- Saída do próximo endereço
    );
END PC4;

ARCHITECTURE Behavioral OF PC4 IS

BEGIN

	PROCESS (clk,reset, Write_Enable)
	BEGIN
		IF (rising_edge(clk)) THEN                      				-- Detecção do Clock
			if (PC_in = "UUUUUUUUUUUUUUUUUUUUUUUUUUUUUUUU") then   	-- Verificação de endereço indefinido
				PC_out <= (others => '0');               			-- Caso indefinido, início no primeiro endereço
			elsif (Write_Enable = '0') then              				-- WriteEnable desabilitado
				PC_out <= PC_in;								-- Manutenção do endereço atual
			elsif (Write_Enable = '1') then						-- WriteEnable habilitado
				PC_out <= PC_in + '1';							-- Atualização do endereço
			end if;
		END IF;
		IF (reset = '1') THEN                           				-- Detecção de Reset
			PC_out <= (others => '0');                   			-- Retorno ao primeiro endereço
		END IF;
	END PROCESS;

END Behavioral;

// VHDL entity Somador, as the project stores it:
LIBRARY ieee;
USE ieee.std_logic_1164.all;
USE IEEE.std_logic_unsigned.ALL; 

ENTITY Somador IS
  PORT (
    A, B        : IN  std_logic_vector(31 DOWNTO 0); 	-- Entrada de vetores de 32 bits
    Z           : OUT std_logic_vector(31 DOWNTO 0) 	-- Saída do vetor resultado da soma
    );
END Somador;

ARCHITECTURE Behavioral OF somador IS

BEGIN

Z <= A + B; 									-- Vetor resultado da soma

END Behavioral;

// VHDL entity RegisterFile, as the project stores it:
library ieee;
use ieee.std_logic_1164.all;
use ieee.numeric_std.all;

entity RegisterFile is
  port(
    Read_Register_1           : in std_logic_vector(4 downto 0);    	-- Endereço do primeiro registrador a ser lido
    Read_Register_2           : in std_logic_vector(4 downto 0);    	-- Endereço do segundo registrador a ser lido
    Write_Register      	    : in std_logic_vector(4 downto 0);    	-- Endereço do registrador a ser escrito
    Write_Data                : in  std_logic_vector(31 downto 0);     -- Dado a ser escrito
    Reg_Write  			    : in  std_logic;     				-- Sinal de controle
    Read_Data_1         	    : out  std_logic_vector(31 downto 0);    -- Dado do primeiro registrador lido
    Read_Data_2       	    : out  std_logic_vector(31 downto 0);    -- Dado do segundo registrador lido
    clk                 	    : in  std_logic                        	-- Sinal do CLOCK
    );
end RegisterFile;

architecture Behavioral of RegisterFile is
  type RegisterFile is array(0 to 31) of std_logic_vector(31 downto 0);
  signal Registers : RegisterFile := 
   ("00000000000000000000000000000000","00000000000000000000000000000000","00000000000000000000000000000000","00000000000000000000000000000000",
    "00000000000000000000000000000000","00000000000000000000000000000000","00000000000000000000000000000000","00000000000000000000000000000000",
    "00000000000000000000000000000000","00000000000000000000000000000000","00000000000000000000000000000000","00000000000000000000000000000000",
    "00000000000000000000000000000000","00000000000000000000000000000000","00000000000000000000000000000000","00000000000000000000000000000000",
    "00000000000000000000000000000000","00000000000000000000000000000000","00000000000000000000000000000000","00000000000000000000000000000000",
    "00000000000000000000000000000000","00000000000000000000000000000000","00000000000000000000000000000000","00000000000000000000000000000000",
    "00000000000000000000000000000000","00000000000000000000000000000000","00000000000000000000000000000000","00000000000000000000000000000000",
    "00000000000000000000000000000000","00000000000000000000000000000000","00000000000000000000000000000000","00000000000000000000000000000000");

begin
  regFile : process (clk) is
  begin
    if falling_edge(CLK) then
      if (Registers(to_integer(unsigned(Read_Register_1))) = "UUUUUUUUUUUUUUUUUUUUUUUUUUUUUUUU") THEN -- Caso o valor do registrador esteja indefinido, a saída será "000..."
      	Read_Data_1 <= (others => '0');  
      ELSE 
      	Read_Data_1 <= registers(to_integer(unsigned(Read_Register_1)));  -- Leitura do valor contido no registrador 1
      END IF;
      IF (Registers(to_integer(unsigned(Read_Register_2))) = "UUUUUUUUUUUUUUUUUUUUUUUUUUUUUUUU") THEN -- Caso o valor do registrador esteja indefinido, a saída será "000..."
      	Read_Data_2 <= (others => '0');  
      ELSE
      	Read_Data_2 <= registers(to_integer(unsigned(Read_Register_2)));  -- Leitura do valor contido no registrador 2 
      END IF;
    end if; 
    if rising_edge(clk) then
      if Reg_Write = '1' then
        Registers(to_integer(unsigned(Write_Register))) <= Write_Data;      -- Escrita do valor no registrador selecionado
      end if;
    end if;
  end process;
  
end Behavioral;

// VHDL entity IFID, as the project stores it:
LIBRARY ieee;
USE ieee.std_logic_1164.all;

ENTITY IFID IS
  PORT (
    clk         : IN  std_logic;                    -- Entrada do CLOCK
    PC_in        : IN  std_logic_vector(31 DOWNTO 0); -- Entrada do valor atual do PC (contador de programa)
    PC4_in	 : IN  std_logic_vector(31 downto 0); -- Entrada do valor do PC mais 4 (próxima instrução)
    Write_Enable   : IN std_logic;                 -- Entrada do sinal de habilitação de escrita no IFID
    Instruction_In      : IN  std_logic_vector(31 DOWNTO 0); -- Entrada da instrução atual buscada na memória de instruções
    PC_out       : OUT std_logic_vector(31 DOWNTO 0); -- Saída do valor atual do PC (contador de programa)
    PC4_out	 : OUT std_logic_vector(31 downto 0); -- Saída do valor do PC mais 4 (próxima instrução)
    Instruction_Out     : OUT std_logic_vector(31 DOWNTO 0);  -- Saída da instrução atual buscada na memória de instruções
    Rs1 : OUT std_logic_vector(4 DOWNTO 0);  -- Saída da instrução atual buscada na memória de instruções
    Rs2 : OUT std_logic_vector(4 DOWNTO 0);  -- Saída da instrução atual buscada na memória de instruções
    Rd : OUT std_logic_vector(4 DOWNTO 0)  -- Saída da instrução atual buscada na memória de instruções
    );
END IFID;


ARCHITECTURE Behavioral OF IFID IS

signal opcode : std_logic_vector(6 downto 0);	-- Opcode da Instrução
signal s_Rs1 : std_logic_vector(4 downto 0);		-- Rs1 da Instrução
signal s_Rs2 : std_logic_vector(4 downto 0);		-- Rs2 da Instrução
signal s_Rd : std_logic_vector(4 downto 0);		-- Rd da Instrução
SIGNAL IDIF : std_logic_vector(117 DOWNTO 0);  	-- Registrador de 96 bits para armazenar os valores do IFID

BEGIN
	-- Definição do Opcode da Instrução
	opcode(0) <= Instruction_In(0);
	opcode(1) <= Instruction_In(1);
	opcode(2) <= Instruction_In(2);
	opcode(3) <= Instruction_In(3);
	opcode(4) <= Instruction_In(4);
	opcode(5) <= Instruction_In(5);
	opcode(6) <= Instruction_In(6);

	process(opcode)
	begin
	-- Rs1
		IF NOT (opcode = "1101111" or opcode = "0110111") THEN  -- Tipos diferentes de U e UJ tem Rs1
		s_Rs1 (0) <= Instruction_In(15);
		s_Rs1 (1) <= Instruction_In(16);
		s_Rs1 (2) <= Instruction_In(17);
		s_Rs1 (3) <= Instruction_In(18);
		s_Rs1 (4) <= Instruction_In(19);
		END IF;

	-- Rs2
		IF (opcode = "0110011" or opcode = "0100011" or opcode = "1100011") THEN  -- Tipos R, S e Sb tem Rs2
		s_Rs2 (0) <= Instruction_In(20);
		s_Rs2 (1) <= Instruction_In(21);
		s_Rs2 (2) <= Instruction_In(22);
		s_Rs2 (3) <= Instruction_In(23);
		s_Rs2 (4) <= Instruction_In(24);
		END IF;

	-- Rd
		IF NOT (opcode = "0100011" or opcode = "1100011") THEN  -- Tipos diferentes de S e Sb tem Rd
		s_Rd (0) <= Instruction_In(7); 
		s_Rd (1) <= Instruction_In(8);
		s_Rd (2) <= Instruction_In(9);
		s_Rd (3) <= Instruction_In(10);
		s_Rd (4) <= Instruction_In(11);
		END IF;
	end process;

	
	PROCESS (clk, Write_Enable)
	BEGIN
		IF (rising_edge(CLK)) THEN                   	-- Detecção de subida de CLOCK
			if (Write_Enable = '1') then             	-- Vericação se o WriteEnable está habilitado
				IDIF(31 DOWNTO 0) <= Instruction_In;       
				IDIF(63 DOWNTO 32) <= PC_in;          	-- Armazena o valor atual do PC
				IDIF(95 downto 64) <= PC4_in;       	-- Armazena o valor do PC mais 4 (próxima instrução)
				IDIF(102 downto 96) <= opcode;		-- Armazena o opcode
				IDIF(107 downto 103) <= s_Rs1;		-- Armazena o Rs1
				IDIF(112 downto 108) <= s_Rs2;		-- Armazena o Rs2
				IDIF(117 downto 113) <= s_Rd;			-- Armazena o Rd
			end if;
		END IF;
		IF (falling_edge(clk)) THEN                 		-- Detecção de descida de CLOCK
			PC_out <= IDIF(63 DOWNTO 32);           	-- Definição do PC atual
			Instruction_Out <= IDIF(31 DOWNTO 0);        -- Definição da instrução armazenada
			PC4_out <= IDIF(95 downto 64);        		-- Saída de PC+4
			Rs1 <= IDIF(107 downto 103);				-- Saída do Rs1
			Rs2 <= IDIF(112 downto 108);				-- Saída do Rs2
			Rd <= IDIF(117 downto 113);				-- Saída do Rd
		END IF;
	END PROCESS;
	
END Behavioral;

// VHDL entity IDEX, as the project stores it:
LIBRARY ieee;
USE ieee.std_logic_1164.all;

ENTITY IDEX IS
  PORT (
    clk             : IN std_logic;                             -- Entrada do sinal de clock            
    ALU_Src_in       : IN std_logic;                             -- Entradas do ALUSrc e ALUOp, que são sinais de controle para a ALU_Control
    ALU_Op_in        : IN std_logic_vector(1 downto 0);          -- ALUSrc e ALUOp são usados no estágio EX do pipeline, então não aparecem nos proximos regs do pipeline
    funct3_in       : IN std_logic_vector(2 downto 0);          -- Entrada do Funct3, usado na ALU_Control
    funct7_in       : IN std_logic_vector(6 downto 0);          -- Entrada do Funct7, usado na ALU_Control
    PC_in           : IN std_logic_vector(31 DOWNTO 0);         -- Entrada do valor atual do PC (contador de programa)
    Soma_PC_in      : IN std_logic;                             -- Entrada do sinal de controle que define quando o PC deve ser somado (jal)        
    Branch_in       : IN std_logic;                             -- Entrada do sinal de controle que define quando ocorre Branch
    Mem_Write_in     : IN std_logic;                             -- Entrada do sinal de controle que define quando a Memória será escrita
    Mem_Read_in      : IN std_logic;                             -- Entrada do sinal de controle que define quando a Memória será lida
    Reg_Write_in     : IN std_logic;                             -- Entrada do sinal de controle que define quando o registrador será escrito
    Mem_To_Reg_in     : IN std_logic;                             -- Entrada do sinal de controle que define quando um dado será passado da memória para o registrador
    read1_in        : IN std_logic_vector(31 DOWNTO 0);         -- Entrada do valor lido do read data 1
    read2_in        : IN std_logic_vector(31 DOWNTO 0);         -- Entrada do valor lido do read data 2
    immediate_in    : in std_logic_vector(31 DOWNTO 0);         -- Entrada do imediato gerado pelo Immediate_Generator
    Rd_in           : IN std_logic_vector(4 DOWNTO 0);          -- Entrada da instrução atual buscada na memória de instruções
    Opcode_in		: IN std_logic_vector(6 DOWNTO 0);		    -- Entrada do Opcode
    JumpReg_in		: IN std_Logic;					    -- Entrada do JumpReg
    Rs1_In		: IN std_logic_vector(4 downto 0);		    -- Entrada do Rs1	
    Rs2_In		: IN std_logic_vector(4 downto 0);		    -- Entrada do Rs2
  
    ALU_Src_out      : out std_logic;                            -- Saídas do ALUSrc e ALUOp, que são sinais de controle para a ALU_Control
    ALU_Op_out       : out std_logic_vector(1 downto 0);         -- ALUSrc e ALUOp são usados no estágio EX do pipeline, então não aparecem nos proximos regs do pipeline
    funct3_out      : out std_logic_vector(2 downto 0);         -- Saída do Funct3, usado na ALU_Control    
    funct7_out      : out std_logic_vector(6 downto 0);         -- Saída do Funct7, usado na ALU_Control
    PC_out          : out std_logic_vector(31 DOWNTO 0);        -- Saída do valor atual do PC (contador de programa)
    Soma_PC_out     : out std_logic;                            -- Saída do sinal de controle que define quando o PC deve ser somado (jal)
    Branch_out      : out std_logic;                            -- Saída do sinal de controle que define quando ocorre Branch
    MemWrite_out    : out std_logic;                            -- Saída do sinal de controle que define quando a Memória será escrita
    Mem_Read_out     : out std_logic;                            -- Saída do sinal de controle que define quando a Memória será lida
    Reg_Write_out    : out std_logic;                            -- Saída do sinal de controle que define quando o registrador será escrito
    Mem_To_Reg_out    : out std_logic;                            -- Saída do sinal de controle que define quando um dado será passado da memória para o registrador
    read1_out       : out std_logic_vector(31 DOWNTO 0);        -- Saída do valor lido do read data 1
    read2_out       : out std_logic_vector(31 DOWNTO 0);        -- Saída do valor lido do read data 2   
    immediate_out   : out std_logic_vector(31 DOWNTO 0);        -- Saída do imediato gerado pelo Immediate_Generator
    Rd_out          : out std_logic_vector(4 DOWNTO 0);         -- Saída da instrução atual buscada na memória de instruções
    Opcode_out		: out std_logic_vector(6 DOWNTO 0);	    -- Saída do Opcode
    JumpReg_out	: out std_Logic;					    -- Saída do JumpReg
    Rs1_out		: out std_logic_vector(4 downto 0);	    -- Saída do Rs1	
    Rs2_out		: out std_logic_vector(4 downto 0)		    -- Saída do Rs2
    );
END IDEX;


ARCHITECTURE Behavioral OF IDEX IS

SIGNAL idex_sig : std_logic_vector(170 DOWNTO 0);  -- Registrador de 151 bits para armazenar os valores do IDEX

BEGIN

    PROCESS (clk)
    BEGIN
        IF (rising_edge(clk)) THEN                   -- Detecção de subida de CLOCK
            idex_sig(0) <= ALU_Src_in;          
            idex_sig(2 downto 1) <= ALU_Op_in;          
            idex_sig(5 DOWNTO 3) <= funct3_in;      
            idex_sig(12 DOWNTO 6) <= funct7_in;
            idex_sig(44 DOWNTO 13) <= PC_in ;  
            idex_sig(45) <= Soma_PC_in;       
            idex_sig(46) <= Branch_in;   
            idex_sig(47) <= Mem_Write_in;   
            idex_sig(48) <= Mem_Read_in;   
            idex_sig(49) <= Reg_Write_in;   
            idex_sig(50) <= Mem_To_Reg_in;   
            idex_sig(82 DOWNTO 51) <= read1_in;    
            idex_sig(114 DOWNTO 83) <= read2_in;    
            idex_sig(146 DOWNTO 115) <= immediate_in;   
            idex_sig(152 DOWNTO 147) <= Rd_in;
            idex_sig(159 downto 153) <= Opcode_in; 
            idex_sig(160) <= JumpReg_in;  
            idex_sig(165 downto 161) <= Rs1_In;
            idex_sig(170 downto 166) <= Rs2_In;      
        END IF;
        IF (falling_edge(clk)) THEN                 -- Detecção de descida de CLOCK
            ALU_Src_out <= idex_sig(0);       
            ALU_Op_out  <= idex_sig(2 downto 1);     
            funct3_out <= idex_sig(5 DOWNTO 3);      
            funct7_out <= idex_sig(12 DOWNTO 6);    
            PC_out <= idex_sig(44 DOWNTO 13);
            Soma_PC_out <= idex_sig(45);
            Branch_out <= idex_sig(46);
            Mem_Write_out <= idex_sig(47);
            Mem_Read_out <= idex_sig(48);
            Reg_Write_out <= idex_sig(49);
            Mem_To_Reg_out <= idex_sig(50);
            read1_out <= idex_sig(82 DOWNTO 51);
            read2_out <= idex_sig(114 DOWNTO 83);
            immediate_out <= idex_sig(146 DOWNTO 115);
            Rd_out <= idex_sig(152 DOWNTO 147);
            Opcode_out <= idex_sig(159 downto 153);
            JumpReg_out <= idex_sig(160);
            Rs1_out <= idex_sig(165 downto 161);
            Rs2_out <= idex_sig(170 downto 166);
        END IF;
    END PROCESS;

    
END Behavioral;

// VHDL entity EXMEM, as the project stores it:
LIBRARY ieee;
USE ieee.std_logic_1164.all;

ENTITY EXMEM IS
  PORT (
    clk             : IN std_logic;                             -- Entrada do sinal de clock            
    Branch_in       : IN std_logic;                             -- Entrada do sinal de controle que define quando ocorre Branch
    Mem_Write_in     : IN std_logic;                             -- Entrada do sinal de controle que define quando a Memória será escrita
    Mem_Read_in      : IN std_logic;                             -- Entrada do sinal de controle que define quando a Memória será lida
    Reg_Write_in     : IN std_logic;                             -- Entrada do sinal de controle que define quando o registrador será escrito
    Mem_To_Reg_in     : IN std_logic;                             -- Entrada do sinal de controle que define quando um dado será passado da memória para o registrador
    New_PC_in       : IN std_logic_vector(31 DOWNTO 0);         -- Soma do PC com imediato (jal) ou reg com imediato substituindo PC (jalr)
    Zero_in         : IN std_logic;                             -- Quando o resultado da ALU foi zero (serve para Branch)
    ALU_result_in    : IN std_logic_vector(31 DOWNTO 0);         -- Entrada do resultado da operação da ALU
    read2_in        : IN std_logic_vector(31 DOWNTO 0);         -- Entrada do valor lido do read data 2
    Rd_in           : IN std_logic_vector(4 DOWNTO 0);          -- Entrada da instrução atual buscada na memória de instruções
    Jalr_ou_Jal_in	: IN std_logic;					    -- Entrada que indica se é Jalr ou Jal	
  
    Branch_out      : out std_logic;                            -- Saída do sinal de controle que define quando ocorre Branch 
    Mem_Write_out    : out std_logic;                            -- Saída do sinal de controle que define quando a Memória será escrita
    Mem_Read_out     : out std_logic;                            -- Saída do sinal de controle que define quando a Memória será lida
    Reg_Write_out    : out std_logic;                            -- Saída do sinal de controle que define quando o registrador será escrito
    Mem_To_Reg_out    : out std_logic;                            -- Saída do sinal de controle que define quando um dado será passado da memória para o registrador
    New_PC_out       : out std_logic_vector(31 DOWNTO 0);        -- Soma do PC com imediato (jal) ou reg com imediato substituindo PC (jalr)
    Zero_out        : out std_logic;                            -- Quando o resultado da ALU foi zero (serve para Branch)
    ALU_result_out   : out std_logic_vector(31 DOWNTO 0);        -- Saída do resultado da operação da ALU
    read2_out       : out std_logic_vector(31 DOWNTO 0);        -- Saída do valor lido do read data 2
    Rd_out          : out std_logic_vector(4 DOWNTO 0);          -- Saída da instrução atual buscada na memória de instruções
    Jalr_ou_Jal_out	: out std_logic					    -- Saída que indica se é Jalr ou Jal
    );
END EXMEM;


ARCHITECTURE Behavioral OF EXMEM IS

SIGNAL exmem_sig : std_logic_vector(107 DOWNTO 0);  -- Registrador de 192 bits para armazenar os valores do EXMEM

BEGIN

    PROCESS (clk)
    BEGIN
        IF (rising_edge(clk)) THEN                   -- Detecta a borda de subida do sinal de clock
            exmem_sig(0)    <= Branch_in;          
            exmem_sig(1)    <= Mem_Write_in;          
            exmem_sig(2)   <= Mem_Read_in;      
            exmem_sig(3)   <= Reg_Write_in;
            exmem_sig(4)   <= Mem_To_Reg_in;  
            exmem_sig(36 downto 5)    <= New_PC_in;       
            exmem_sig(37)           <= Zero_in;   
            exmem_sig(69 downto 38)    <= ALU_result_in;   
            exmem_sig(101 downto 70)    <= read2_in;   
            exmem_sig(106 downto 102)    <= Rd_in;   
            exmem_sig(107) <= Jalr_ou_Jal_in;
        END IF;
        IF (falling_edge(clk)) THEN                 -- Detecta a borda de descida do sinal de clock
            Branch_out    <= exmem_sig(0);       
            Mem_Write_out  <= exmem_sig(1);     
            Mem_Read_out  <= exmem_sig(2);      
            Reg_Write_out <= exmem_sig(3);    
            Mem_To_Reg_out <= exmem_sig(4);
            New_PC_out <= exmem_sig(36 downto 5);
            Zero_out <= exmem_sig(37);
            ALU_result_out <= exmem_sig(69 downto 38);
            read2_out <= exmem_sig(101 downto 70);
            Rd_out <= exmem_sig(106 downto 102);
            Jalr_ou_Jal_out <= exmem_sig(107);
        END IF;
    END PROCESS;

    
END Behavioral;

// VHDL entity Hazard, as the project stores it:
library IEEE;
use IEEE.STD_LOGIC_1164.ALL;

entity Hazard is 
    port( 
        clk                 : IN std_logic;                          -- Entrada do sinal de clock
        Mem_Read_in          : IN std_logic;                          -- Sinal de controle que define quando a Memória será lida
        Rd_EX               : IN std_logic_vector(4 downto 0);       -- Rd é o endereço de destino da operação feita pelo CPU após o estágio de EX
        Rs1, Rs2            : IN std_logic_vector(4 downto 0);       -- Rs1 e Rs2 são os endereços dos registradores contidos na instrução
        stall               : OUT std_logic                          -- Saída que indica se um "stall" (atraso) deve ser aplicado no pipeline
    );
end Hazard;

architecture Behavioral of Hazard is

    signal stall_interno : std_logic := '0';  -- Signal temporário que armazena o nível lógico do stall

begin
    process(clk)
    begin
        if ((MemRead_in = '1') and ((Rd_EX = Rs1) or (Rd_EX = Rs2))) then        -- Fórmula do livro, página 322
            stall_interno <= '1';                                                -- Se o sinal de controle de MemRead_in for igual a 1 e o resultado  
        end if;                                                                  -- do estágio de Execution estiver em Rs1 ou Rs2, realiza um stall
    end process;

    stall <= stall_interno;                                                     -- Atribui o valor do signal temporário stall_interno à saída stall

end Behavioral;

// VHDL entity Forward, as the project stores it:
library IEEE;
use IEEE.STD_LOGIC_1164.ALL;

entity Forward is 
    port( 
         clk                        : IN std_logic;                         -- Entrada do sinal de clock
         reg_Write_WB, regWrite_MEM  : IN std_logic;                         -- Sinais de controle de escrita no registrador do WB e do Mem, respectivamente
         Rs1, Rs2                   : IN std_logic_vector(4 downto 0);      -- Endereçoes dos registradores Rs1 e Rs2 vindos do estágio ID/EX do pipeline
         Rd_WB, Rd_Mem              : IN std_logic_vector(4 downto 0);      -- Endereços dos registradores de armazenamento Rd, vindos dos estágios de MEM/WB e EX/MEM do pipeline
         forwardA, forwardB         : OUT std_logic_vector(1 downto 0)      -- Saídas indicando os forwards para as fontes A e B
     );
end Forward;

ARCHITECTURE TypeArchitecture OF MEMWB IS
    signal forwardA_interno, forwardB_interno : std_logic_vector(1 downto 0) := "00";   -- Sinais internos que armazenam o encaminhamento

begin
    process(clk)
    begin
        if ((regWrite_MEM = '1') and (not(Rd_Mem = "00000")) and (Rd_Mem = Rs1)) then
            forwardA_interno <= "10";   
        end if;

        if ((regWrite_MEM = '1') and (not(Rd_Mem = "00000")) and (Rd_Mem = Rs2)) then
            forwardB_interno <= "10";  
        end if;

        if ((regWrite_WB = '1') and (not(Rd_WB = "00000")) and (Rd_WB = Rs1)) then
            forwardA_interno <= "01";   
        end if;

        if ((regWrite_WB = '1') and (not(Rd_WB = "00000")) and (Rd_WB = Rs2)) then
            forwardB_interno <= "01";   
        end if;

    end process;

    forwardA <= forwardA_interno;  
    forwardB <= forwardB_interno;
       
END TypeArchitecture;

// VHDL entity MEMWB, as the project stores it:
LIBRARY ieee;
USE ieee.std_logic_1164.all;

ENTITY MEMWB IS
  PORT (
    CLK             : IN std_logic;                             -- Entrada do sinal de clock            
    RegWrite_in     : IN std_logic;                             -- Entrada do sinal de controle que define quando o registrador será escrito
    MemToReg_in     : IN std_logic;                             -- Entrada do sinal de controle que define quando um dado será passado da memória para o registrador
    Mem_data_in     : IN std_logic_vector(31 DOWNTO 0);         -- Entrada do valor lido na memória
    ALUresult_in    : IN std_logic_vector(31 DOWNTO 0);         -- Entrada do resultado da operação da ALU
    Rd_in           : IN std_logic_vector(4 DOWNTO 0);          -- Entrada da instrução atual buscada na memória de instruções
  
    RegWrite_out    : out std_logic;                            -- Saída do sinal de controle que define quando o registrador será escrito
    MemToReg_out    : out std_logic;                            -- Saída do sinal de controle que define quando um dado será passado da memória para o registrador
    Mem_data_out    : out std_logic_vector(31 DOWNTO 0);        -- Saída do valor lido na memória
    ALUresult_out   : out std_logic_vector(31 DOWNTO 0);        -- Saída do resultado da operação da ALU
    Rd_out          : out std_logic_vector(4 DOWNTO 0)          -- Saída da instrução atual buscada na memória de instruções
    );
END MEMWB;


ARCHITECTURE TypeArchitecture OF MEMWB IS

SIGNAL memwb_sig : std_logic_vector(70 DOWNTO 0);  -- Registrador de 70 bits para armazenar os valores do memwb

BEGIN

    PROCESS (CLK)
    BEGIN
        IF (rising_edge(CLK)) THEN                   -- Detecta a borda de subida do sinal de clock     
            memwb_sig(0)   <= RegWrite_in;
            memwb_sig(1)   <= MemToReg_in;  
            memwb_sig(33 downto 2)  <= Mem_data_in ;       
            memwb_sig(65 downto 34)  <= ALUresult_in;   
            memwb_sig(70 downto 66)  <= Rd_in;   
        END IF;
        IF (falling_edge(CLK)) THEN                 -- Detecta a borda de descida do sinal de clock
            RegWrite_out <= memwb_sig(0);    
            MemToReg_out <= memwb_sig(1);
            Mem_data_out <= memwb_sig(33 downto 2);
            ALUresult_out <= memwb_sig(65 downto 34);
            Rd_out <= memwb_sig(70 downto 66);
        END IF;
    END PROCESS;

    
END TypeArchitecture;
